# Fritzing sketch licenta (saved by Fritzing 0.9.4)
breadboards: 1

parts:
  Part1 = Arduino Uno (Rev3)
  M3 = Getriebemotor
  M4 = Getriebemotor
  M5 = Getriebemotor
  M6 = Getriebemotor
  L298N1 = L298N DC motor driver
  BAT1 = BC9VPC [package=bc9vpc]
  BAT2 = BC9VPC [package=bc9vpc]
  Q2 = TRANSISTOR_NPN [package=to-92-ammo]
  Q3 = Basic FET N-Channel [package="TO220 [THT]"]
  A1 = Hanmatek HM305
  R1 = Resistor [tolerance=±5% resistance=1k package="2512 [SMD]"]
  R2 = Resistor [tolerance=±5% resistance=10k package="2512 [SMD]"]  # not connected
  L1 = Inductor [package="400 mil [THT]"]
  D1 = Schottky Diode [part_number=1N5817 package="Melf DO-213 AB [SMD]"]
  C1 = Electrolytic Capacitor [capacitance=0.47mF voltage=20V package="100 mil [THT, electrolytic]"]
  D2 = Schottky Diode [part_number=1N5817 package="Melf DO-213 AB [SMD]"]
  INA1 = INA219 DC Current Sensor Breakout
  R3 = Resistor [tolerance=±5% resistance=22k package="2512 [SMD]"]
  R4 = Resistor [tolerance=±5% resistance=10k package="2512 [SMD]"]

nets:
  N1: Part1.A0, R1.Pin_0
  N2: Part1.A1, R3.Pin_1, R4.Pin_0
  N3: M3.pin_1, M4.pin_1, L298N1.OUT4
  N4: M3.pin_2, M4.pin_2, L298N1.OUT3
  N5: M5.pin_1, M6.pin_1, L298N1.OUT2
  N6: M5.pin_2, M6.pin_2, L298N1.OUT1
  N7: L298N1.12V, BAT1.V+, BAT2.V+
  N8: L298N1.GND, BAT1.V-, BAT2.V-
  N9: Q2.E, A1.Pin_3, L1.pin_1, D1.anode, C1.-, C1.+, D2.anode, R4.Pin_1
  N10: Q2.B, R1.Pin_1
  N11: Q2.C, Q3.gate
  N12: Q3.drain, INA1.Vin-2
  N13: Q3.source, L1.pin_0, D1.cathode
  N14: A1.Pin_4, INA1.Vin+2
  N15: D2.cathode, R3.Pin_0

custom parts:
  L298N DC motor driver: 2x DC motor driver with 78M05 positive voltage regulator (7..35 V) L298N: max 46 V, 2 A Set 5 V Enable jumper to enable 5 V regultor (needed for the L298N) and +5 V output at screw terminal or supply external +5 V at screw terminal Set ENA and/or ENB to +5 V to enable motor permanently or supply ENA and/or ENB with PWM signal IN1 and IN2 set rotation directory for motor A (OUT1/OUT2) IN2 and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
  Hanmatek HM305: DC Power Supply 30V5A HM305.
  INA219 DC Current Sensor Breakout: INA DC Current Sensor Breakout

// code stored in the sketch: getcurrent.ino
#include <Wire.h>
#include <Adafruit_INA219.h>

Adafruit_INA219 ina219;


void setup(void) 
{
  Serial.begin(115200);
  while (!Serial) {
      // will pause Zero, Leonardo, etc until serial console opens
      delay(1);
  }
    
  Serial.println("Hello!");
  
  // Initialize the INA219.
  // By default the initialization will use the largest range (32V, 2A).  However
  // you can call a setCalibration function to change this range (see comments).
  if (! ina219.begin()) {
    Serial.println("Failed to find INA219 chip");
    while (1) { delay(10); }
  }
  // To use a slightly lower 32V, 1A range (higher precision on amps):
  //ina219.setCalibration_32V_1A();
  // Or to use a lower 16V, 400mA range (higher precision on volts and amps):
  //ina219.setCalibration_16V_400mA();

  Serial.println("Measuring voltage and current with INA219 ...");
}

void loop(void) 
{
  float shuntvoltage = 0;
  float busvoltage = 0;
  float current_mA = 0;
  float loadvoltage = 0;
  float power_mW = 0;

  shuntvoltage = ina219.getShuntVoltage_mV();
  busvoltage = ina219.getBusVoltage_V();
  current_mA = ina219.getCurrent_mA();
  power_mW = ina219.getPower_mW();
  loadvoltage = busvoltage + (shuntvoltage / 1000);
  
  Serial.print("Bus Voltage:   "); Serial.print(busvoltage); Serial.println(" V");
  Serial.print("Shunt Voltage: "); Serial.print(shuntvoltage); Serial.println(" mV");
  Serial.print("Load Voltage:  "); Serial.print(loadvoltage); Serial.println(" V");
  Serial.print("Current:       "); Serial.print(current_mA); Serial.println(" mA");
  Serial.print("Power:         "); Serial.print(power_mW); Serial.println(" mW");
  Serial.println("");

  delay(2000);
}
