# Fritzing sketch proiect_incipient (saved by Fritzing 0.9.4)
breadboards: 1

parts:
  Part1 = Arduino Uno (Rev3)
  Mod1 = ESP32 - CAM
  LED1 = LED - 5mm [color="Red (633nm)" package="5 mm [THT]"]
  LED2 = LED - 5mm [color="Green (555nm)" package="5 mm [THT]"]
  R1 = Resistor [tolerance=±5% resistance=10k package=THT]
  Q1 = Basic FET N-Channel [package="TO220 [THT]"]
  Part2 = FC-03
  Part3 = FC-03
  C1 = Ceramic Capacitor [capacitance=100nF package="100 mil [THT, multilayer]"]
  C2 = Ceramic Capacitor [capacitance=100nF package="100 mil [THT, multilayer]"]  # not connected

nets:
  N1: Part1.A0, Mod1.IO12
  N2: Part1.A1, Mod1.IO13
  N3: Part1.A2, Mod1.IO15
  N4: Part1.A3, Mod1.IO14
  N5: Part1.A4/SDA, Mod1.IO2
  N6: Part1.A5/SCL, Mod1.IO4
  N7: Part1.D8, LED2.anode
  N8: Part1.D13/SCK, LED1.cathode
  N9: Part1.D2, Part3.D0
  N10: Part1.D3_PWM, Part2.D0, C1.1
  5V: Part1.5V, Part1.VIN, Mod1.5V, Q1.gate, Part2.VCC, Part3.VCC
  GND: Part1.GND, Mod1.GND, R1.Pin_1, Q1.drain, Part2.GND, Part3.GND, C1.0
  N11: LED1.anode, LED2.cathode, R1.Pin_0

custom parts:
  ESP32 - CAM: The ESP32-CAM has a very competitive small-size camera module that can operate independently as a minimum system with a footprint of only 27*40.5*4.5mm and a deep sleep current of up to 6mA.
  FC-03: FC-03, LM393 IR Speed Sensor Encoder By Nandan
